# Fritzing sketch Skema (saved by Fritzing 0.9.3b)

parts:
  M1 = DOIT Esp32 DevKit v1 (30 pins long, 11 pins width) [part_number=ESP32S-PIN30]
  A1 = 2957N11 pressure sensor
  Part2 = Adafruit MAX31865 RTD Sensor Breakout [part_number="Adafruit #3328"]
  U1 = LM2596 step down module
  VALVE1 = Plastic Solenoid Valve
  OLED_I2C1 = OLED 128x64 I2C Monochrome Display
  J1 = Basic Servo
  R1 = Resistor [tolerance=±5% resistance=10k package="0402 [SMD]"]
  R2 = Resistor [tolerance=±5% resistance=10k package="0603 [SMD]"]
  S1 = Momentary Switch [package=ksa_sealed_tac_switch]
  S2 = Momentary Switch [package=ksa_sealed_tac_switch]
  S3 = Momentary Switch [package=ksa_sealed_tac_switch]
  JACK1 = 2.1mm Barrel Jack with Terminal Block
  2_Channel_Relay1 = 2 Channel Power Relay
  J3 = female pin header, 2 pins [form="♀ (female)"]
  R3 = Resistor [tolerance=±5% resistance=10k package="0603 [SMD]"]
  J2 = female pin header, 2 pins [form="♀ (female)"]
  A2 = 2957N11 pressure sensor
  Bat1 = Battery

nets:
  3V3: M1.3V3, Part2.3.3V, OLED_I2C1.VDD
  GND: M1.GND, A1.Pin_1, Part2.GND, U1.IN-, U1.OUT-, OLED_I2C1.GND, J1.gnd, R2.Pin_1, S1.4, S2.4, S3.4, JACK1.NEG, 2_Channel_Relay1.GND, 2_Channel_Relay1.K1-COM
  N1: M1.D4, J1.pulse
  N2: M1.D5, Part2.CS
  N3: M1.D18, Part2.SCLK
  N4: M1.D19, Part2.SDO
  N5: M1.D21, OLED_I2C1.SDA
  N6: M1.D22, OLED_I2C1.SCK
  N7: M1.D23, Part2.SDI
  N8: M1.D34, R1.Pin_1, R3.Pin_0
  N9: M1.D32, S3.1
  N10: M1.D33, S2.1
  N11: M1.D25, S1.1
  N12: M1.D26, 2_Channel_Relay1.IN2
  N13: M1.D27, 2_Channel_Relay1.IN1
  VCC: M1.VIN, A1.Pin_2, U1.OUT+, J1.vcc, 2_Channel_Relay1.VCC
  N14: A1.Pin_3, R1.Pin_0
  N15: Part2.RTDIN+, Part2.FORCE+, A2.Pin_2, A2.Pin_3
  N16: Part2.FORCE-, Part2.RTDIN-, A2.Pin_1
  N17: U1.IN+, VALVE1.no_name_yet#1, JACK1.POS
  N18: VALVE1.no_name_yet#2, 2_Channel_Relay1.K1-NO
  N19: 2_Channel_Relay1.K2-COM, J3.pin1
  N20: 2_Channel_Relay1.K2-NO, J3.pin2
  N21: J2.pin1, Bat1.-
  N22: J2.pin2, Bat1.+

custom parts:
  DOIT Esp32 DevKit v1 (30 pins long, 11 pins width): The DOIT Esp32 DevKit v1 is one of the development board created by DOIT to evaluate the ESP-WROOM-32 module. It is based on the ESP32 microcontroller that boasts Wifi, Bluetooth, Ethernet and Low Power support all in a single chip. (vanepp) made breadboard work, adjusted pin numbering and labels and reduced size of schematic and cleaned up pcb. This chip is 30pins long (2 x15) and 11 pins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
  2957N11 pressure sensor: Monitor and control vacuum pumps, air compressors, and hydraulics. These transmitters convert both pressure and vacuum into an electrical signal that can be interpreted by receiving devices, such as remote displays, programmable logic controllers, and motor speed controls.
  Adafruit MAX31865 RTD Sensor Breakout: For precision temperature sensing, nothing beats a Platinum RTD. Resistance temperature detectors (RTDs) are temperature sensors that contain a resistor that changes resistance value as its temperature changes, basically a kind of thermistor. In this sensor, the resistor is actually a small strip of Platinum with a resistance of 100 ohms at 0°C, thus the name PT100. Compared to most NTC/PTC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
  LM2596 step down module: LM2596 DC-DC step down power supply module 3 A.
  2 Channel Power Relay: A 2 channel power relay. The module operates at 5V.
