# Fritzing sketch pcb (saved by Fritzing 0.9.3b)
circuit board: 11.0023cm x 10.3742cm

parts:
  ESP_32 = DOIT Esp32 DevKit v1 (30 pins long, 11 pins width) [part_number=ESP32S-PIN30]
  Power_12V = molex pin header, 2 pins [form=molex]
  Oled-PushButton = molex pin header, 7 pins [form=molex]
  Stepdown_5V = LM2596 step down module
  Relay = molex pin header, 4 pins [form=molex]
  part = female pin header, 1 pin [form="♀ (female)"]
  Sensor_Tekanan = molex pin header, 3 pins [form=molex]
  Resistor_10kΩ = female pin header, 1 pin [form="♀ (female)"]
  Resistor_20kΩ = female pin header, 1 pin [form="♀ (female)"]
  Max31865 = molex pin header, 6 pins [form=molex]
  Servo = molex pin header, 3 pins [form=molex]
  part_2 = female pin header, 1 pin [form="♀ (female)"]
  part_3 = female pin header, 1 pin [form="♀ (female)"]
  J5 = female pin header, 1 pin [form="♀ (female)"]
  J6 = female pin header, 1 pin [form="♀ (female)"]
  J7 = female pin header, 1 pin [form="♀ (female)"]
  J8 = female pin header, 1 pin [form="♀ (female)"]

nets:
  N1: ESP_32.3V3, Oled-PushButton.pin1, Max31865.pin1
  N2: ESP_32.GND, Stepdown_5V.OUT+, Relay.pin2, Resistor_20kΩ.pin1, Max31865.pin2, Servo.pin2
  N3: ESP_32.D4, J5.pin1
  N4: ESP_32.D5, Max31865.pin3
  N5: ESP_32.D18, Max31865.pin4
  N6: ESP_32.D19, Max31865.pin5
  N7: ESP_32.D21, Oled-PushButton.pin4
  N8: ESP_32.D22, Oled-PushButton.pin3
  N9: ESP_32.D23, Max31865.pin6
  N10: ESP_32.D34, Resistor_10kΩ.pin1
  N11: ESP_32.D32, Oled-PushButton.pin7
  N12: ESP_32.D33, Oled-PushButton.pin6
  N13: ESP_32.D25, Oled-PushButton.pin5
  N14: ESP_32.D26, Relay.pin3
  N15: ESP_32.D27, Relay.pin4
  N16: ESP_32.VIN, Relay.pin1, Servo.pin1, part_2.pin1
  N17: Power_12V.pin1, Stepdown_5V.IN+
  N18: Power_12V.pin2, Oled-PushButton.pin2, Stepdown_5V.IN-, Stepdown_5V.OUT-, Sensor_Tekanan.pin1, Sensor_Tekanan.pin2, part_3.pin1
  N19: part.pin1, Sensor_Tekanan.pin3
  N20: Servo.pin3, J7.pin1
  N21: J6.pin1, J8.pin1

custom parts:
  DOIT Esp32 DevKit v1 (30 pins long, 11 pins width): The DOIT Esp32 DevKit v1 is one of the development board created by DOIT to evaluate the ESP-WROOM-32 module. It is based on the ESP32 microcontroller that boasts Wifi, Bluetooth, Ethernet and Low Power support all in a single chip. (vanepp) made breadboard work, adjusted pin numbering and labels and reduced size of schematic and cleaned up pcb. This chip is 30pins long (2 x15) and 11 pins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
  LM2596 step down module: LM2596 DC-DC step down power supply module 3 A.
